# Fritzing sketch WiFi Extender (saved by Fritzing 1.0.6)
breadboards: 1

parts:
  Mod1 = Amica NodeMCU DEVKIT 1.0
  Grove1 = Grove OLED 128x96
  LED1 = RGB LED (com. anode, rbg) [color="Red (633nm)" current=0.030A package="5 mm [THT]"]
  R1 = Resistor [tolerance=±5% resistance=220 package="2010 [SMD]"]
  R2 = Resistor [tolerance=±5% resistance=220 package="2010 [SMD]"]
  R3 = Resistor [tolerance=±5% resistance=220 package="2010 [SMD]"]
  U1 = LIPO-2000mAh [package=lipo-2000]

nets:
  N1: Mod1.pin1, Mod1.pin_26, Grove1.VCC
  N2: Mod1.pin2, Mod1.pin_9, Mod1.pin_25, Mod1.pin_29, Grove1.GND, LED1.common_anode, U1.-
  N3: Mod1.pin6, R3.Pin_1
  N4: Mod1.pin7, R2.Pin_1
  N5: Mod1.pin8, R1.Pin_0
  N6: Mod1.pin_13, Grove1.SDA
  N7: Mod1.pin_14, Grove1.SCL
  N8: Mod1.pin_30, U1.+
  N9: LED1.red_cathode, R1.Pin_1
  N10: LED1.blue_cathode, R2.Pin_0
  N11: LED1.green_cathode, R3.Pin_0
